# Fritzing sketch shield-3615-v2 (saved by Fritzing 0.9.3b)
circuit board: 6.88566cm x 5.36311cm
breadboards: 1

parts:
  1μF = Electrolytic Capacitor [capacitance=1µF voltage=50V package="100 mil [THT, electrolytic]"]
  10kΩ = Resistor [tolerance=±5% resistance=10k package=THT]
  USB-A = USB Connectors [package=usb-a-h]
  10µF = Electrolytic Capacitor [capacitance=10µF voltage=50V package="100 mil [THT, electrolytic]"]
  L7805CV = Voltage Regulator - 5V [package="TO220 [THT]"]
  Composant1 = Arduino Uno (Rev3)
  J1 = female pin header, 4 pins [form="♀ (female)"]
  Level_Converter = Logic Level Converter

nets:
  GND: 1μF.-, USB-A.GND, 10µF.-, L7805CV.GND, Composant1.GND, J1.pin2, Level_Converter.GND
  5V: 1μF.+, 10kΩ.Pin_1, L7805CV.output_voltage, Composant1.5V, Level_Converter.HV
  N1: 10kΩ.Pin_0, USB-A.D-, Composant1.D8
  N2: USB-A.D+, Composant1.D9_PWM
  N3: USB-A.VBUS, 10µF.+, L7805CV.input_voltage
  N4: Composant1.D0/RX, Level_Converter.RX2_HV
  N5: Composant1.D1/TX, Level_Converter.TX2_HV
  3.3V: Composant1.3V3, J1.pin1, Level_Converter.LV
  N6: J1.pin3, Level_Converter.RX2_LV
  N7: J1.pin4, Level_Converter.TX2_LV

notes:
  This work is licensed under a Creative Commons Attribution-ShareAlike 4.0 International License.
  http://3615.entropie.org
  3615 v2
  Entropie 2017
  5V
  GND
  3V3
  TX0'
  RX0'
  Level
  Converter
