# Fritzing sketch shield-3615 (saved by Fritzing 0.9.3b)
circuit board: 6.88566cm x 5.36311cm
breadboards: 1

parts:
  C4 = Electrolytic Capacitor [capacitance=10µF voltage=25V package="100 mil [THT, electrolytic]"]
  R1 = Resistor [tolerance=±5% resistance=10k package=THT]
  USB-A = USB Connectors [package=usb-a-h]
  C1 = Electrolytic Capacitor [capacitance=100µF voltage=25V package="100 mil [THT, electrolytic]"]
  7805 = Voltage Regulator - 5V [package="TO220 [THT]"]
  Composant1 = Arduino Uno (Rev3)
  J1 = female pin header, 4 pins [form="♀ (female)"]
  Level_Converter = Logic Level Converter
  C3 = Ceramic Capacitor [capacitance=100nF voltage=35V package="200 mil [THT, multilayer]"]
  C2 = Ceramic Capacitor [capacitance=330nF voltage=35V package="200 mil [THT, multilayer]"]

nets:
  GND: C4.-, USB-A.GND, C1.-, 7805.GND, Composant1.GND, J1.pin2, Level_Converter.GND, C3.0, C2.0
  5V: C4.+, R1.Pin_1, 7805.output_voltage, Composant1.5V, Level_Converter.HV, C3.1
  N1: R1.Pin_0, USB-A.D-, Composant1.D8
  N2: USB-A.D+, Composant1.D9_PWM
  N3: USB-A.VBUS, C1.+, 7805.input_voltage, C2.1
  N4: Composant1.D0/RX, Level_Converter.RX2_HV
  N5: Composant1.D1/TX, Level_Converter.TX2_HV
  3.3V: Composant1.3V3, J1.pin1, Level_Converter.LV
  N6: J1.pin3, Level_Converter.RX2_LV
  N7: J1.pin4, Level_Converter.TX2_LV

notes:
  This work is licensed under a Creative Commons Attribution-ShareAlike 4.0 International License.
  http://3615.entropie.org
  3615
  Entropie 2017
  5V
  GND
  3V3
  TX0'
  RX0'
  Level
  Converter
